// Logisim project lab8.circ as structural Verilog: 7 circuits, main circuit Adder1b
module Adder1b (
  input  A,
  input  B,
  input  Cin,
  output S,
  output Cout
);

  wire and_1_out, and_2_out, and_3_out, xor_1_out;

  xor xor_1 (xor_1_out, A, B);
  and and_1 (and_1_out, A, B);
  and and_2 (and_2_out, B, Cin);
  and and_3 (and_3_out, A, Cin);
  xor xor_2 (S, xor_1_out, Cin);
  or or_1 (Cout, and_1_out, and_2_out, and_3_out);
endmodule

module AddSub4b (
  input  [3:0] A,
  input  [3:0] B,
  input  Ctrl,
  output [3:0] S,
  output Cout
);

  wire m0_cout, m1_cout, m2_cout, m3_cout, xor_1_out, xor_2_out, xor_3_out, xor_4_out;

  xor xor_1 (xor_1_out, B[0], Ctrl);
  xor xor_2 (xor_2_out, B[1], Ctrl);
  xor xor_3 (xor_3_out, B[2], Ctrl);
  xor xor_4 (xor_4_out, B[3], Ctrl);
  Adder1b m0 (.A(A[0]), .B(xor_1_out), .Cin(Ctrl), .S(S[0]), .Cout(m0_cout));
  Adder1b m1 (.A(A[1]), .B(xor_2_out), .Cin(m0_cout), .S(S[1]), .Cout(m1_cout));
  Adder1b m2 (.A(A[2]), .B(xor_3_out), .Cin(m1_cout), .S(S[2]), .Cout(m2_cout));
  Adder1b m3 (.A(A[3]), .B(xor_4_out), .Cin(m2_cout), .S(S[3]), .Cout(m3_cout));
  xor xor_5 (Cout, m3_cout, Ctrl);
endmodule

module And2b4 (
  input  [3:0] A,
  input  [3:0] B,
  output [3:0] res
);

  and and_1 (res[0], A[0], B[0]);
  and and_2 (res[1], A[1], B[1]);
  and and_3 (res[2], A[2], B[2]);
  and and_4 (res[3], A[3], B[3]);
endmodule

module Or2b4 (
  input  [3:0] A,
  input  [3:0] B,
  output [3:0] res
);

  or or_1 (res[0], A[0], B[0]);
  or or_2 (res[1], A[1], B[1]);
  or or_3 (res[2], A[2], B[2]);
  or or_4 (res[3], A[3], B[3]);
endmodule

module ALU (
  input  [3:0] A,
  input  [3:0] B,
  input  [1:0] op,
  output [3:0] res,
  output Cout
);

  wire m0_cout;
  wire [3:0] m0_s, m1_res, m2_res;

  AddSub4b m0 (.A(A), .B(B), .Ctrl(op[0]), .S(m0_s), .Cout(m0_cout));
  And2b4 m1 (.A(A), .B(B), .res(m1_res));
  Or2b4 m2 (.A(A), .B(B), .res(m2_res));
  Mux4to1b4 m3 (.S(op), .I0(m0_s), .I1(m0_s), .I2(m1_res), .I3(m2_res), .O(res));
  Mux4to1 m4 (.S(op), .D0(m0_cout), .D1(m0_cout), .D2(1'b0), .D3(1'b0), .Y(Cout));
endmodule

module Mux4to1 (
  input  [1:0] S,
  input  D0,
  input  D1,
  input  D2,
  input  D3,
  output Y
);

  wire and_1_out, and_2_out, and_3_out, and_4_out, and_5_out, and_6_out, and_7_out, and_8_out, not_1_out,
       not_2_out;

  not not_1 (not_1_out, S[0]);
  not not_2 (not_2_out, S[1]);
  and and_1 (and_1_out, not_1_out, not_2_out);
  and and_2 (and_2_out, S[0], not_2_out);
  and and_3 (and_3_out, not_1_out, S[1]);
  and and_4 (and_4_out, S[0], S[1]);
  and and_5 (and_5_out, and_1_out, D0);
  and and_6 (and_6_out, and_2_out, D1);
  and and_7 (and_7_out, and_3_out, D2);
  and and_8 (and_8_out, and_4_out, D3);
  or or_1 (Y, and_5_out, and_6_out, and_7_out, and_8_out);
endmodule

module Mux4to1b4 (
  input  [1:0] S,
  input  [3:0] I0,
  input  [3:0] I1,
  input  [3:0] I2,
  input  [3:0] I3,
  output [3:0] O
);

  Mux4to1 O0 (.S(S), .D0(I0[0]), .D1(I1[0]), .D2(I2[0]), .D3(I3[0]), .Y(O[0]));
  Mux4to1 O1 (.S(S), .D0(I0[1]), .D1(I1[1]), .D2(I2[1]), .D3(I3[1]), .Y(O[1]));
  Mux4to1 O2 (.S(S), .D0(I0[2]), .D1(I1[2]), .D2(I2[2]), .D3(I3[2]), .Y(O[2]));
  Mux4to1 O3 (.S(S), .D0(I0[3]), .D1(I1[3]), .D2(I2[3]), .D3(I3[3]), .Y(O[3]));
endmodule
