// Logisim project lab6.circ as structural Verilog: 2 circuits, main circuit MyMC14495
module MyMC14495 (
  input  LE,
  input  Point,
  input  D0,
  input  D1,
  input  D2,
  input  D3,
  output p,
  output g,
  output f,
  output e,
  output d,
  output c,
  output b,
  output a
);

  wire and_1_out, and_2_out, and_3_out, and_4_out, and_5_out, and_6_out, and_7_out, and_8_out, and_9_out,
       and_10_out, and_11_out, and_12_out, and_13_out, and_14_out, and_15_out, and_16_out, and_17_out,
       and_18_out, and_19_out, and_20_out, and_21_out, not_2_out, not_3_out, not_4_out, not_5_out, or_1_out,
       or_3_out, or_6_out, or_7_out, or_9_out, or_12_out, or_14_out;

  not not_1 (p, Point);
  and and_1 (and_1_out, not_2_out, not_3_out, D2, D3);
  and and_2 (and_2_out, D0, D1, D2, not_5_out);
  or or_1 (or_1_out, and_1_out, and_2_out, and_3_out);
  or or_2 (g, LE, or_1_out);
  and and_3 (and_3_out, not_3_out, not_4_out, not_5_out);
  and and_4 (and_4_out, D0, D1, not_5_out);
  and and_5 (and_5_out, D1, not_4_out, not_5_out);
  or or_3 (or_3_out, and_4_out, and_5_out, and_6_out, and_19_out);
  or or_4 (f, LE, or_3_out);
  and and_6 (and_6_out, D0, not_4_out, not_5_out);
  and and_7 (and_7_out, D0, not_3_out, not_4_out);
  or or_5 (e, LE, or_6_out);
  and and_8 (and_8_out, not_3_out, D2, not_5_out);
  or or_6 (or_6_out, and_7_out, and_8_out, and_9_out);
  and and_9 (and_9_out, D0, not_5_out);
  and and_10 (and_10_out, not_2_out, D1, not_4_out, D3);
  and and_11 (and_11_out, D0, D1, D2);
  or or_7 (or_7_out, and_10_out, and_11_out, and_20_out, and_21_out);
  or or_8 (d, LE, or_7_out);
  and and_12 (and_12_out, D1, D2, D3);
  and and_13 (and_13_out, not_2_out, D1, not_4_out, not_5_out);
  or or_9 (or_9_out, and_12_out, and_13_out, and_15_out);
  or or_10 (c, LE, or_9_out);
  and and_14 (and_14_out, D0, D1, D3);
  and and_15 (and_15_out, not_2_out, D2, D3);
  and and_16 (and_16_out, not_2_out, D1, D2);
  or or_11 (b, LE, or_12_out);
  and and_17 (and_17_out, D0, not_3_out, D2, not_5_out);
  or or_12 (or_12_out, and_14_out, and_15_out, and_16_out, and_17_out);
  and and_18 (and_18_out, D0, D1, not_4_out, D3);
  not not_2 (not_2_out, D0);
  and and_19 (and_19_out, D0, not_3_out, D2, D3);
  not not_3 (not_3_out, D1);
  and and_20 (and_20_out, not_2_out, not_3_out, D2, not_5_out);
  or or_13 (a, LE, or_14_out);
  not not_4 (not_4_out, D2);
  not not_5 (not_5_out, D3);
  and and_21 (and_21_out, D0, not_4_out, not_3_out, not_5_out);
  or or_14 (or_14_out, and_18_out, and_19_out, and_20_out, and_21_out);
endmodule

module DispNum (
  input  [1:0] BTN,
  input  [7:0] SW,
  output [7:0] SEGMENT,
  output [3:0] AN,
  output BTN_X
);

  not not_1 (AN[0], SW[4]);
  not not_2 (AN[1], SW[5]);
  not not_3 (AN[2], SW[6]);
  not not_4 (AN[3], SW[7]);
  MyMC14495 MC14495 (
    .LE(BTN[0]), .Point(BTN[1]), .D0(SW[0]), .D1(SW[1]), .D2(SW[2]), .D3(SW[3]), .p(SEGMENT[7]),
    .g(SEGMENT[6]), .f(SEGMENT[5]), .e(SEGMENT[4]), .d(SEGMENT[3]), .c(SEGMENT[2]), .b(SEGMENT[1]),
    .a(SEGMENT[0]));

  assign BTN_X = 1'b0;
endmodule
