// Logisim project LAB5_D_74LS138.circ as structural Verilog: 3 circuits, main circuit D_74LS138
module D_74LS138 (
  input  A,
  input  B,
  input  C,
  input  G,
  input  G2A,
  input  G2B,
  output [7:0] Y
);

  wire and_1_out, and_2_out, and_3_out, and_4_out, nor_1_out, not_1_out, not_2_out, not_3_out, not_4_out;

  not not_1 (not_1_out, A);
  not not_2 (not_2_out, B);
  not not_3 (not_3_out, C);
  not not_4 (not_4_out, G);
  and and_1 (and_1_out, not_1_out, not_2_out);
  and and_2 (and_2_out, A, not_2_out);
  and and_3 (and_3_out, not_1_out, B);
  and and_4 (and_4_out, A, B);
  nor nor_1 (nor_1_out, not_4_out, G2A, G2B);
  nand nand_1 (Y[0], and_1_out, nor_1_out, not_3_out);
  nand nand_2 (Y[1], and_2_out, nor_1_out, not_3_out);
  nand nand_3 (Y[2], and_3_out, nor_1_out, not_3_out);
  nand nand_4 (Y[3], and_4_out, nor_1_out, not_3_out);
  nand nand_5 (Y[4], and_1_out, nor_1_out, C);
  nand nand_6 (Y[5], and_2_out, nor_1_out, C);
  nand nand_7 (Y[6], and_3_out, nor_1_out, C);
  nand nand_8 (Y[7], nor_1_out, and_4_out, C);
endmodule

module D_74LS138_TEST (
  input  [5:0] in_1,
  output [7:0] out_2
);

  D_74LS138 d_74ls138_1 (.A(in_1[0]), .B(in_1[1]), .C(in_1[2]), .G(in_1[3]), .G2A(in_1[4]), .G2B(in_1[5]), .Y(out_2));
endmodule

module LampCtrl138 (
  input  S1,
  input  S2,
  input  S3,
  output F
);

  wire [7:0] d_74ls138_1_y;

  D_74LS138 d_74ls138_1 (.A(S1), .B(S2), .C(S3), .G(1'b1), .G2A(1'b0), .G2B(1'b0), .Y(d_74ls138_1_y));
  nand nand_1 (F, d_74ls138_1_y[1], d_74ls138_1_y[2], d_74ls138_1_y[4], d_74ls138_1_y[7]);
endmodule
