// Logisim project lab9.circ as structural Verilog: 5 circuits, main circuit SR_latch
module SR_latch (
  input  R,
  input  S,
  output Q,
  output Qbar
);

  nor nor_1 (Q, R, Qbar);
  nor nor_2 (Qbar, Q, S);
endmodule

module C_SR_latch (
  input  R,
  input  C,
  input  S,
  output Qbar,
  output Q
);

  wire nand_1_out, nand_2_out;

  nand nand_1 (nand_1_out, R, C);
  nand nand_2 (nand_2_out, C, S);
  nand nand_3 (Qbar, nand_1_out, Q);
  nand nand_4 (Q, Qbar, nand_2_out);
endmodule

module C_D_latch (
  input  D,
  input  C,
  output Qbar,
  output Q
);

  wire nand_1_out, nand_2_out, not_1_out;

  not not_1 (not_1_out, D);
  nand nand_1 (nand_1_out, not_1_out, C);
  nand nand_2 (nand_2_out, C, D);
  nand nand_3 (Qbar, nand_1_out, Q);
  nand nand_4 (Q, Qbar, nand_2_out);
endmodule

module MS_SR_flip_flop (
  input  R,
  input  S,
  input  clk,
  output mid_Q,
  output Qbar,
  output Q
);

  wire master_latch_qbar, not_1_out;

  not not_1 (not_1_out, clk);
  C_SR_latch master_latch (.R(R), .C(clk), .S(S), .Qbar(master_latch_qbar), .Q(mid_Q));
  C_SR_latch slave_latch (.R(master_latch_qbar), .C(not_1_out), .S(mid_Q), .Qbar(Qbar), .Q(Q));
endmodule

module ET_D_flip_flop (
  input  clk,
  input  D,
  output Q,
  output Qbar
);

  wire nand_1_out, nand_2_out, nand_3_out, nand_4_out;

  nand nand_1 (nand_1_out, nand_4_out, nand_2_out);
  nand nand_2 (nand_2_out, nand_1_out, clk);
  nand nand_3 (nand_3_out, nand_2_out, clk, nand_4_out);
  nand nand_4 (nand_4_out, nand_3_out, D);
  nand nand_5 (Q, nand_2_out, Qbar);
  nand nand_6 (Qbar, Q, nand_3_out);
endmodule
